# Fritzing sketch LED01 (saved by Fritzing 0.9.3b)
breadboards: 1

parts:
  LED1 = LED - 5mm [color="Red (633nm)" package="5 mm [THT]"]
  U1 = NodeMCU V1.0
  R1 = Resistor [tolerance=±5% resistance=220 package=THT]

nets:
  N1: LED1.cathode, U1.GND
  N2: LED1.anode, R1.Pin_0
  N3: U1.D2, R1.Pin_1

custom parts:
  NodeMCU V1.0: ESP8266 based NodeMCU
