# Fritzing sketch LED02 (saved by Fritzing 0.9.3b)
breadboards: 1

parts:
  R1 = Resistor [tolerance=±5% resistance=220 package=THT]
  R2 = Resistor [tolerance=±5% resistance=220 package=THT]
  U1 = NodeMCU V1.0
  LED1 = LED - 5mm [color="Red (633nm)" package="5 mm [THT]"]
  LED2 = LED - 5mm [color="Yellow (595nm)" package="5 mm [THT]"]

nets:
  N1: R1.Pin_0, LED1.anode
  N2: R1.Pin_1, U1.D2
  N3: R2.Pin_0, LED2.anode
  N4: R2.Pin_1, U1.D4
  N5: U1.GND, LED1.cathode

custom parts:
  NodeMCU V1.0: ESP8266 based NodeMCU
