# Fritzing sketch LED03 (saved by Fritzing 0.9.3b)
breadboards: 1

parts:
  R1 = Resistor [tolerance=±5% resistance=220 package=THT]
  LED1 = LED - 5mm [color="Red (633nm)" package="5 mm [THT]"]
  LED2 = LED - 5mm [color="Yellow (595nm)" package="5 mm [THT]"]
  LED3 = LED - 5mm [color="Blue (525nm)" package="5 mm [THT]"]
  R2 = Resistor [tolerance=±5% resistance=220 package=THT]
  R3 = Resistor [tolerance=±5% resistance=220 package=THT]
  U1 = NodeMCU V1.0

nets:
  N1: R1.Pin_0, LED1.anode
  N2: R1.Pin_1, U1.D2
  N3: LED1.cathode, LED2.cathode, LED3.cathode, U1.GND
  N4: LED2.anode, R2.Pin_0
  N5: LED3.anode, R3.Pin_0
  N6: R2.Pin_1, U1.D4
  N7: R3.Pin_1, U1.D6

custom parts:
  NodeMCU V1.0: ESP8266 based NodeMCU
